# Fritzing sketch circuit (saved by Fritzing 0.9.1b)
breadboards: 1

parts:
  Raspberry_Pi1 = Raspberry Pi B+
  C1 = Capacitor Polarized [package=cpol-radial-10uf-25v]
  U1 = OP482 - Low Power, High Speed JFET Quad Operational Amplifier [part_number=OP482]
  JACK1 = 2.1mm Barrel Jack with Terminal Block
  NEOPIXEL1 = Neopixel Strip -- Black (30/m)

nets:
  N1: Raspberry_Pi1.GPIO18, U1.-INA
  GND: Raspberry_Pi1.GND, C1.+, U1.OUTA, U1.OUTB, JACK1.NEG, NEOPIXEL1.GND
  5V: Raspberry_Pi1.5V, C1.-, U1.OUTD, JACK1.POS, NEOPIXEL1.+5V
  N2: U1.+INA, NEOPIXEL1.Din

custom parts:
  Neopixel Strip -- Black (30/m): These NeoPixel strips have 30 digitally-addressable pixel LEDs per meter and are very affordable and are only 12.5 mm wide, 10 mm if you remove the strip from the casing.
